// Logisim project SAP-1 computer.circ as structural Verilog: 10 circuits, main circuit main
module main (
  input  Clear,
  output [3:0] out_2,
  output [3:0] out_3,
  output Output0,
  output Output1,
  output Output2,
  output Output3,
  output Output4,
  output Output5,
  output Output6,
  output Output7
);

  wire controle_1_cp, controle_1_ep, controle_1_halt, controle_1_nce, controle_1_nei, controle_1_nli,
       controle_1_nlm, controlled_buffer_1_out, CP_out, Ea, Eu, nLa, nLb, nLo, not_1_out, not_2_out,
       not_3_out, not_4_out, not_5_out, not_6_out, not_7_out, not_8_out, Su;
  wire [3:0] registrador_4_bits_1607066_1_y0, registrador_8_bits_1607066_1_y0,
       registrador_8_bits_1607066_1_y4;
  wire [7:0] adder_subtructor_1_output, bit_extender_1_out, registrador_8_bits_1607066_2_y0,
       registrador_8_bits_1607066_3_y0, xor_1_out;

  not not_1 (not_1_out, controle_1_halt);
  assign controlled_buffer_1_out = not_1_out ? CP_out : 1'bz;  // Controlled_Buffer controlled_buffer_1
  Clock CP (.out(CP_out));
  not not_2 (not_2_out, controle_1_nlm);
  controle controle_1 (
    .Clock(controlled_buffer_1_out), .Clear(Clear), .HALT(controle_1_halt),
    .Input(registrador_8_bits_1607066_1_y4), .CP(controle_1_cp), .EP(controle_1_ep), .nLM(controle_1_nlm),
    .nCE(controle_1_nce), .nLi(controle_1_nli), .nEi(controle_1_nei), .nLA(nLa), .EA(Ea), .SU(Su), .EU(Eu),
    .nLB(nLb), .nLo(nLo));
  contador_1607066 contador_1607066_1 (
    .c0(out_3[3]), .c1(out_3[2]), .c2(out_3[1]), .c3(out_3[0]), .Count(controle_1_cp), .CLR(Clear),
    .CP(controlled_buffer_1_out), .ENABLE(controle_1_ep));
  Registrador_4_bits__1607066 registrador_4_bits_1607066_1 (
    .X3(out_3[3]), .X2(out_3[2]), .X1(out_3[1]), .X0(out_3[0]), .Y3(registrador_4_bits_1607066_1_y0[3]),
    .Y2(registrador_4_bits_1607066_1_y0[2]), .Y1(registrador_4_bits_1607066_1_y0[1]),
    .Y0(registrador_4_bits_1607066_1_y0[0]), .LOAD(not_2_out), .CLK(controlled_buffer_1_out), .CLR(Clear),
    .ENABLE(1'b1));
  Registrador_8_bits___1607066 registrador_8_bits_1607066_1 (
    .X7(out_2[3]), .X6(out_2[2]), .X5(out_2[1]), .X4(out_2[0]), .X3(out_3[3]), .X2(out_3[2]), .X1(out_3[1]),
    .X0(out_3[0]), .Y7(registrador_8_bits_1607066_1_y4[3]), .Y6(registrador_8_bits_1607066_1_y4[2]),
    .Y5(registrador_8_bits_1607066_1_y4[1]), .Y4(registrador_8_bits_1607066_1_y4[0]),
    .Y3(registrador_8_bits_1607066_1_y0[3]), .Y2(registrador_8_bits_1607066_1_y0[2]),
    .Y1(registrador_8_bits_1607066_1_y0[1]), .Y0(registrador_8_bits_1607066_1_y0[0]), .LOAD(not_3_out),
    .CLK(controlled_buffer_1_out), .CLR(Clear), .ENABLE(1'b1));
  not not_3 (not_3_out, controle_1_nli);
  RAM #(.addrWidth(4)) ram_1 (
    .addr(registrador_4_bits_1607066_1_y0), .data({out_2, out_3}), .sel(not_4_out),
    .clk(controlled_buffer_1_out));  // open: ld, clr
  not not_4 (not_4_out, controle_1_nce);
  assign out_3 = not_5_out ? registrador_8_bits_1607066_1_y0 : 4'bz;  // Controlled_Buffer controlled_buffer_2
  not not_5 (not_5_out, controle_1_nei);
  assign {out_2, out_3} = Ea ? registrador_8_bits_1607066_2_y0 : 8'bz;  // Controlled_Buffer controlled_buffer_3
  assign {out_2, out_3} = Eu ? adder_subtructor_1_output : 8'bz;  // Controlled_Buffer controlled_buffer_4
  Registrador_8_bits___1607066 registrador_8_bits_1607066_2 (
    .X7(out_2[3]), .X6(out_2[2]), .X5(out_2[1]), .X4(out_2[0]), .X3(out_3[3]), .X2(out_3[2]), .X1(out_3[1]),
    .X0(out_3[0]), .Y7(registrador_8_bits_1607066_2_y0[7]), .Y6(registrador_8_bits_1607066_2_y0[6]),
    .Y5(registrador_8_bits_1607066_2_y0[5]), .Y4(registrador_8_bits_1607066_2_y0[4]),
    .Y3(registrador_8_bits_1607066_2_y0[3]), .Y2(registrador_8_bits_1607066_2_y0[2]),
    .Y1(registrador_8_bits_1607066_2_y0[1]), .Y0(registrador_8_bits_1607066_2_y0[0]), .LOAD(not_7_out),
    .CLK(controlled_buffer_1_out), .CLR(Clear), .ENABLE(1'b1));
  Adder_Subtructor adder_subtructor_1 (
    .B(xor_1_out), .A(registrador_8_bits_1607066_2_y0), .Cin(Su), .Output(adder_subtructor_1_output));  // open: out_5
  not not_6 (not_6_out, nLb);
  Registrador_8_bits___1607066 registrador_8_bits_1607066_3 (
    .X7(out_2[3]), .X6(out_2[2]), .X5(out_2[1]), .X4(out_2[0]), .X3(out_3[3]), .X2(out_3[2]), .X1(out_3[1]),
    .X0(out_3[0]), .Y7(registrador_8_bits_1607066_3_y0[7]), .Y6(registrador_8_bits_1607066_3_y0[6]),
    .Y5(registrador_8_bits_1607066_3_y0[5]), .Y4(registrador_8_bits_1607066_3_y0[4]),
    .Y3(registrador_8_bits_1607066_3_y0[3]), .Y2(registrador_8_bits_1607066_3_y0[2]),
    .Y1(registrador_8_bits_1607066_3_y0[1]), .Y0(registrador_8_bits_1607066_3_y0[0]), .LOAD(not_6_out),
    .CLK(controlled_buffer_1_out), .CLR(Clear), .ENABLE(1'b1));
  Registrador_8_bits___1607066 registrador_8_bits_1607066_4 (
    .X7(out_2[3]), .X6(out_2[2]), .X5(out_2[1]), .X4(out_2[0]), .X3(out_3[3]), .X2(out_3[2]), .X1(out_3[1]),
    .X0(out_3[0]), .Y7(Output7), .Y6(Output6), .Y5(Output5), .Y4(Output4), .Y3(Output3), .Y2(Output2),
    .Y1(Output1), .Y0(Output0), .LOAD(not_8_out), .CLK(controlled_buffer_1_out), .CLR(Clear), .ENABLE(1'b1));
  not not_7 (not_7_out, nLa);
  assign xor_1_out = registrador_8_bits_1607066_3_y0 ^ bit_extender_1_out;  // XOR_Gate xor_1, 8 bits wide
  not not_8 (not_8_out, nLo);
  assign bit_extender_1_out = {{7{Su}}, Su};  // Bit_Extender bit_extender_1
  Hex_Digit_Display hex_digit_display_1 (.value({Output7, Output6, Output5, Output4}));  // open: dp
  Hex_Digit_Display hex_digit_display_2 (.value({Output3, Output2, Output1, Output0}));  // open: dp
endmodule

module Registrador_8_bits (
  input  X7,
  input  X6,
  input  X5,
  input  X4,
  input  X3,
  input  X2,
  input  X1,
  input  X0,
  input  LOAD,
  input  CLR,
  input  CLK,
  input  Enable,
  output Y7,
  output Y6,
  output Y5,
  output Y4,
  output Y3,
  output Y2,
  output Y1,
  output Y0
);

  wire and_1_out, and_2_out, and_3_out, and_4_out, and_5_out, and_6_out, and_7_out, and_8_out, and_9_out,
       and_10_out, and_11_out, and_12_out, and_13_out, and_14_out, and_15_out, and_16_out, d_ff_1_q,
       d_ff_2_q, d_ff_3_q, d_ff_4_q, d_ff_5_q, d_ff_6_q, d_ff_7_q, d_ff_8_q, not_1_out, not_2_out, or_1_out,
       or_2_out, or_3_out, or_4_out, or_5_out, or_6_out, or_7_out, or_8_out;

  and and_1 (and_1_out, d_ff_1_q, not_1_out);
  and and_2 (and_2_out, X7, LOAD);
  or or_1 (or_1_out, and_1_out, and_2_out);
  D_Flip_Flop d_ff_1 (.clk(CLK), .D(or_1_out), .Q(d_ff_1_q), .reset(CLR));  // open: Qn, preset, en
  Registrador_4_bits__1607066 registrador_4_bits_1607066_1 (
    .X3(CLK), .X2(CLK), .Y3(CLK), .CLR(CLR), .ENABLE(CLR));  // open: X1, X0, Y2, Y1, Y0, LOAD, CLK
  assign Y7 = Enable ? d_ff_1_q : 1'bz;  // Controlled_Buffer controlled_buffer_1
  and and_3 (and_3_out, d_ff_2_q, not_1_out);
  and and_4 (and_4_out, X6, LOAD);
  or or_2 (or_2_out, and_3_out, and_4_out);
  D_Flip_Flop d_ff_2 (.clk(CLK), .D(or_2_out), .Q(d_ff_2_q), .reset(CLR));  // open: Qn, preset, en
  assign Y6 = Enable ? d_ff_2_q : 1'bz;  // Controlled_Buffer controlled_buffer_2
  and and_5 (and_5_out, d_ff_3_q, not_1_out);
  or or_3 (or_3_out, and_5_out, and_6_out);
  and and_6 (and_6_out, X5, LOAD);
  D_Flip_Flop d_ff_3 (.clk(CLK), .D(or_3_out), .Q(d_ff_3_q), .reset(CLR));  // open: Qn, preset, en
  assign Y5 = Enable ? d_ff_3_q : 1'bz;  // Controlled_Buffer controlled_buffer_3
  and and_7 (and_7_out, d_ff_4_q, not_1_out);
  or or_4 (or_4_out, and_7_out, and_8_out);
  and and_8 (and_8_out, X4, LOAD);
  D_Flip_Flop d_ff_4 (.clk(CLK), .D(or_4_out), .Q(d_ff_4_q), .reset(CLR));  // open: Qn, preset, en
  assign Y4 = Enable ? d_ff_4_q : 1'bz;  // Controlled_Buffer controlled_buffer_4
  not not_1 (not_1_out, LOAD);
  and and_9 (and_9_out, d_ff_5_q, not_2_out);
  or or_5 (or_5_out, and_9_out, and_10_out);
  and and_10 (and_10_out, X3, LOAD);
  D_Flip_Flop d_ff_5 (.clk(CLK), .D(or_5_out), .Q(d_ff_5_q), .reset(CLR));  // open: Qn, preset, en
  assign Y3 = Enable ? d_ff_5_q : 1'bz;  // Controlled_Buffer controlled_buffer_5
  and and_11 (and_11_out, X2, LOAD);
  and and_12 (and_12_out, d_ff_6_q, not_2_out);
  or or_6 (or_6_out, and_12_out, and_11_out);
  D_Flip_Flop d_ff_6 (.clk(CLK), .D(or_6_out), .Q(d_ff_6_q), .reset(CLR));  // open: Qn, preset, en
  assign Y2 = Enable ? d_ff_6_q : 1'bz;  // Controlled_Buffer controlled_buffer_6
  and and_13 (and_13_out, X1, LOAD);
  and and_14 (and_14_out, d_ff_7_q, not_2_out);
  or or_7 (or_7_out, and_14_out, and_13_out);
  D_Flip_Flop d_ff_7 (.clk(CLK), .D(or_7_out), .Q(d_ff_7_q), .reset(CLR));  // open: Qn, preset, en
  assign Y1 = Enable ? d_ff_7_q : 1'bz;  // Controlled_Buffer controlled_buffer_7
  and and_15 (and_15_out, X0, LOAD);
  and and_16 (and_16_out, d_ff_8_q, not_2_out);
  or or_8 (or_8_out, and_16_out, and_15_out);
  D_Flip_Flop d_ff_8 (.clk(CLK), .D(or_8_out), .Q(d_ff_8_q), .reset(CLR));  // open: Qn, preset, en
  assign Y0 = Enable ? d_ff_8_q : 1'bz;  // Controlled_Buffer controlled_buffer_8
  not not_2 (not_2_out, LOAD);
endmodule

module somador_1607066 (
  input  X,
  input  Y,
  input  Z,
  output S,
  output C
);

  wire and_1_out, and_2_out, xor_1_out;

  xor xor_1 (xor_1_out, X, Y);
  and and_1 (and_1_out, X, Y);
  xor xor_2 (S, xor_1_out, Z);
  and and_2 (and_2_out, xor_1_out, Z);
  or or_1 (C, and_2_out, and_1_out);
endmodule

module Adder_Subtructor (
  input  [7:0] B,
  input  [7:0] A,
  input  Cin,
  output [7:0] Output,
  output out_5
);

  wire somador_1607066_1_c, somador_1607066_2_c, somador_1607066_3_c, somador_1607066_4_c,
       somador_1607066_5_c, somador_1607066_6_c, somador_1607066_7_c;

  somador_1607066 somador_1607066_1 (.X(B[0]), .Y(A[0]), .Z(Cin), .S(Output[0]), .C(somador_1607066_1_c));
  somador_1607066 somador_1607066_2 (
    .X(B[1]), .Y(A[1]), .Z(somador_1607066_1_c), .S(Output[1]), .C(somador_1607066_2_c));
  somador_1607066 somador_1607066_3 (
    .X(B[2]), .Y(A[2]), .Z(somador_1607066_2_c), .S(Output[2]), .C(somador_1607066_3_c));
  somador_1607066 somador_1607066_4 (
    .X(B[3]), .Y(A[3]), .Z(somador_1607066_3_c), .S(Output[3]), .C(somador_1607066_4_c));
  somador_1607066 somador_1607066_5 (
    .X(B[4]), .Y(A[4]), .Z(somador_1607066_4_c), .S(Output[4]), .C(somador_1607066_5_c));
  somador_1607066 somador_1607066_6 (
    .X(B[5]), .Y(A[5]), .Z(somador_1607066_5_c), .S(Output[5]), .C(somador_1607066_6_c));
  somador_1607066 somador_1607066_7 (
    .X(B[6]), .Y(A[6]), .Z(somador_1607066_6_c), .S(Output[6]), .C(somador_1607066_7_c));
  somador_1607066 somador_1607066_8 (.X(B[7]), .Y(A[7]), .Z(somador_1607066_7_c), .S(Output[7]), .C(out_5));
endmodule

module Registrador_4_bits__1607066 (
  input  X3,
  input  X2,
  input  X1,
  input  X0,
  input  LOAD,
  input  CLK,
  input  CLR,
  input  ENABLE,
  output Y3,
  output Y2,
  output Y1,
  output Y0
);

  wire AND_1_out, AND_2_out, AND_3_out, AND_4_out, AND_5_out, AND_6_out, AND_7_out, AND_8_out, d_ff_1_q,
       d_ff_2_q, d_ff_3_q, d_ff_4_q, NOT_1_out, OR_1_out, OR_2_out, OR_3_out, OR_4_out;

  and AND_2 (AND_2_out, d_ff_1_q, NOT_1_out);
  or OR_1 (OR_1_out, AND_2_out, AND_1_out);
  D_Flip_Flop d_ff_1 (.clk(CLK), .D(OR_1_out), .Q(d_ff_1_q), .reset(CLR));  // open: Qn, preset, en
  and AND_1 (AND_1_out, X3, LOAD);
  assign Y3 = ENABLE ? d_ff_1_q : 1'bz;  // Controlled_Buffer TRI_STATE_1
  and AND_3 (AND_3_out, d_ff_2_q, NOT_1_out);
  and AND_4 (AND_4_out, X2, LOAD);
  or OR_2 (OR_2_out, AND_3_out, AND_4_out);
  D_Flip_Flop d_ff_2 (.clk(CLK), .D(OR_2_out), .Q(d_ff_2_q), .reset(CLR));  // open: Qn, preset, en
  assign Y2 = ENABLE ? d_ff_2_q : 1'bz;  // Controlled_Buffer TRI_STATE_2
  and AND_5 (AND_5_out, d_ff_3_q, NOT_1_out);
  or OR_3 (OR_3_out, AND_5_out, AND_6_out);
  D_Flip_Flop d_ff_3 (.clk(CLK), .D(OR_3_out), .Q(d_ff_3_q), .reset(CLR));  // open: Qn, preset, en
  and AND_6 (AND_6_out, X1, LOAD);
  assign Y1 = ENABLE ? d_ff_3_q : 1'bz;  // Controlled_Buffer TRI_STATE_3
  and AND_7 (AND_7_out, d_ff_4_q, NOT_1_out);
  D_Flip_Flop d_ff_4 (.clk(CLK), .D(OR_4_out), .Q(d_ff_4_q), .reset(CLR));  // open: Qn, preset, en
  not NOT_1 (NOT_1_out, LOAD);
  and AND_8 (AND_8_out, X0, LOAD);
  or OR_4 (OR_4_out, AND_7_out, AND_8_out);
  assign Y0 = ENABLE ? d_ff_4_q : 1'bz;  // Controlled_Buffer TRI_STATE_4
endmodule

module Registrador_8_bits___1607066 (
  input  X7,
  input  X6,
  input  X5,
  input  X4,
  input  X3,
  input  X2,
  input  X1,
  input  X0,
  input  LOAD,
  input  CLK,
  input  CLR,
  input  ENABLE,
  output Y7,
  output Y5,
  output Y4,
  output Y3,
  output Y2,
  output Y1,
  output Y0,
  output Y6
);

  wire AND_1_out, AND_2_out, AND_3_out, AND_4_out, AND_5_out, AND_6_out, AND_7_out, AND_8_out, AND_9_out,
       AND_10_out, AND_11_out, AND_12_out, AND_13_out, AND_14_out, AND_15_out, AND_16_out, d_ff_1_q,
       d_ff_2_q, d_ff_3_q, d_ff_4_q, d_ff_5_q, d_ff_6_q, d_ff_7_q, d_ff_8_q, NOT_1_out, OR_1_out, OR_2_out,
       OR_3_out, OR_4_out, OR_5_out, OR_6_out, OR_7_out, OR_8_out;

  and AND_2 (AND_2_out, d_ff_1_q, NOT_1_out);
  or OR_1 (OR_1_out, AND_2_out, AND_1_out);
  D_Flip_Flop d_ff_1 (.clk(CLK), .D(OR_1_out), .Q(d_ff_1_q), .reset(CLR));  // open: Qn, preset, en
  and AND_1 (AND_1_out, X7, LOAD);
  assign Y7 = ENABLE ? d_ff_1_q : 1'bz;  // Controlled_Buffer TRI_STATE_1
  and AND_3 (AND_3_out, d_ff_2_q, NOT_1_out);
  and AND_4 (AND_4_out, X6, LOAD);
  or OR_2 (OR_2_out, AND_3_out, AND_4_out);
  D_Flip_Flop d_ff_2 (.clk(CLK), .D(OR_2_out), .Q(d_ff_2_q), .reset(CLR));  // open: Qn, preset, en
  assign Y6 = ENABLE ? d_ff_2_q : 1'bz;  // Controlled_Buffer TRI_STATE_2
  and AND_5 (AND_5_out, d_ff_3_q, NOT_1_out);
  or OR_3 (OR_3_out, AND_5_out, AND_6_out);
  D_Flip_Flop d_ff_3 (.clk(CLK), .D(OR_3_out), .Q(d_ff_3_q), .reset(CLR));  // open: Qn, preset, en
  and AND_6 (AND_6_out, X5, LOAD);
  assign Y5 = ENABLE ? d_ff_3_q : 1'bz;  // Controlled_Buffer TRI_STATE_3
  and AND_7 (AND_7_out, d_ff_4_q, NOT_1_out);
  D_Flip_Flop d_ff_4 (.clk(CLK), .D(OR_4_out), .Q(d_ff_4_q), .reset(CLR));  // open: Qn, preset, en
  and AND_8 (AND_8_out, X4, LOAD);
  or OR_4 (OR_4_out, AND_7_out, AND_8_out);
  assign Y4 = ENABLE ? d_ff_4_q : 1'bz;  // Controlled_Buffer TRI_STATE_4
  and AND_10 (AND_10_out, X3, LOAD);
  and AND_9 (AND_9_out, d_ff_5_q, NOT_1_out);
  or OR_5 (OR_5_out, AND_9_out, AND_10_out);
  D_Flip_Flop d_ff_5 (.clk(CLK), .D(OR_5_out), .Q(d_ff_5_q), .reset(CLR));  // open: Qn, preset, en
  assign Y3 = ENABLE ? d_ff_5_q : 1'bz;  // Controlled_Buffer TRI_STATE_5
  and AND_11 (AND_11_out, d_ff_6_q, NOT_1_out);
  or OR_6 (OR_6_out, AND_11_out, AND_12_out);
  D_Flip_Flop d_ff_6 (.clk(CLK), .D(OR_6_out), .Q(d_ff_6_q), .reset(CLR));  // open: Qn, preset, en
  and AND_12 (AND_12_out, X2, LOAD);
  assign Y2 = ENABLE ? d_ff_6_q : 1'bz;  // Controlled_Buffer TRI_STATE_6
  and AND_13 (AND_13_out, d_ff_7_q, NOT_1_out);
  and AND_14 (AND_14_out, X1, LOAD);
  or OR_7 (OR_7_out, AND_13_out, AND_14_out);
  D_Flip_Flop d_ff_7 (.clk(CLK), .D(OR_7_out), .Q(d_ff_7_q), .reset(CLR));  // open: Qn, preset, en
  assign Y1 = ENABLE ? d_ff_7_q : 1'bz;  // Controlled_Buffer TRI_STATE_7
  and AND_15 (AND_15_out, d_ff_8_q, NOT_1_out);
  or OR_8 (OR_8_out, AND_15_out, AND_16_out);
  D_Flip_Flop d_ff_8 (.clk(CLK), .D(OR_8_out), .Q(d_ff_8_q), .reset(CLR));  // open: Qn, preset, en
  not NOT_1 (NOT_1_out, LOAD);
  and AND_16 (AND_16_out, X0, LOAD);
  assign Y0 = ENABLE ? d_ff_8_q : 1'bz;  // Controlled_Buffer TRI_STATE_8
endmodule

module contador_1607066 (
  input  Count,
  input  CLR,
  input  CP,
  input  ENABLE,
  output c0,
  output c1,
  output c3,
  output c2
);

  wire AND_1_2_out, AND_1_out, AND_2_out, j_k_ff_1_q, j_k_ff_2_q, j_k_ff_3_q, j_k_ff_4_q;

  and AND_1 (AND_1_out, Count, AND_2_out, j_k_ff_2_q);
  J_K_Flip_Flop j_k_ff_1 (.J(AND_1_out), .clk(CP), .K(AND_1_out), .Q(j_k_ff_1_q), .reset(CLR));  // open: Qn, preset, en
  assign c0 = ENABLE ? j_k_ff_1_q : 1'bz;  // Controlled_Buffer TRI_STATE_1
  and AND_2 (AND_2_out, Count, AND_1_2_out, j_k_ff_3_q);
  and AND_1_2 (AND_1_2_out, Count, j_k_ff_4_q);
  J_K_Flip_Flop j_k_ff_2 (.J(AND_2_out), .clk(CP), .K(AND_2_out), .Q(j_k_ff_2_q), .reset(CLR));  // open: Qn, preset, en
  assign c1 = ENABLE ? j_k_ff_2_q : 1'bz;  // Controlled_Buffer TRI_STATE_2
  J_K_Flip_Flop j_k_ff_3 (
    .J(AND_1_2_out), .clk(CP), .K(AND_1_2_out), .Q(j_k_ff_3_q), .reset(CLR));  // open: Qn, preset, en
  assign c2 = ENABLE ? j_k_ff_3_q : 1'bz;  // Controlled_Buffer TRI_STATE_3
  J_K_Flip_Flop j_k_ff_4 (.J(Count), .clk(CP), .K(Count), .Q(j_k_ff_4_q), .reset(CLR));  // open: Qn, preset, en
  assign c3 = ENABLE ? j_k_ff_4_q : 1'bz;  // Controlled_Buffer TRI_STATE_4
endmodule

module sap_1_contador_anel (
  input  Clock,
  input  Clear,
  output T1,
  output T5,
  output T6,
  output T2,
  output T3,
  output T4
);

  wire j_k_ff_1_q, j_k_ff_2_qn, j_k_ff_3_qn, j_k_ff_4_qn, j_k_ff_5_qn, j_k_ff_6_qn, not_1_out;

  not not_1 (not_1_out, Clock);
  J_K_Flip_Flop j_k_ff_1 (
    .J(j_k_ff_6_qn), .clk(not_1_out), .K(T6), .Q(j_k_ff_1_q), .Qn(T1), .reset(Clear));  // open: preset, en
  J_K_Flip_Flop j_k_ff_2 (
    .J(T1), .clk(not_1_out), .K(j_k_ff_1_q), .Q(T2), .Qn(j_k_ff_2_qn), .reset(Clear));  // open: preset, en
  J_K_Flip_Flop j_k_ff_3 (
    .J(T2), .clk(not_1_out), .K(j_k_ff_2_qn), .Q(T3), .Qn(j_k_ff_3_qn), .reset(Clear));  // open: preset, en
  J_K_Flip_Flop j_k_ff_4 (
    .J(T3), .clk(not_1_out), .K(j_k_ff_3_qn), .Q(T4), .Qn(j_k_ff_4_qn), .reset(Clear));  // open: preset, en
  J_K_Flip_Flop j_k_ff_5 (
    .J(T4), .clk(not_1_out), .K(j_k_ff_4_qn), .Q(T5), .Qn(j_k_ff_5_qn), .reset(Clear));  // open: preset, en
  J_K_Flip_Flop j_k_ff_6 (
    .J(T5), .clk(not_1_out), .K(j_k_ff_5_qn), .Q(T6), .Qn(j_k_ff_6_qn), .reset(Clear));  // open: preset, en
endmodule

module decodificador (
  input  Input_0,
  input  Input_1,
  input  Input_2,
  input  Input_3,
  output LDA,
  output ADD,
  output SUB,
  output OUT,
  output HLT
);

  wire not_1_out, not_2_out, not_3_out, not_4_out;

  not not_1 (not_1_out, Input_3);
  not not_2 (not_2_out, Input_2);
  not not_3 (not_3_out, Input_1);
  not not_4 (not_4_out, Input_0);
  and and_1 (LDA, not_4_out, not_3_out, not_2_out, not_1_out);
  and and_2 (ADD, Input_0, not_3_out, not_2_out, not_1_out);
  and and_3 (SUB, not_4_out, Input_1, not_2_out, not_1_out);
  and and_4 (OUT, not_4_out, Input_1, Input_2, Input_3);
  and and_5 (HLT, Input_0, Input_1, Input_2, Input_3);
endmodule

module controle (
  input  Clock,
  input  [3:0] Input,
  input  Clear,
  output HALT,
  output EP,
  output CP,
  output nLo,
  output EA,
  output SU,
  output nLB,
  output nEi,
  output nLA,
  output EU,
  output nLi,
  output nLM,
  output nCE
);

  wire and_1_out, and_2_out, and_3_out, and_4_out, and_5_out, and_6_out, and_7_out, and_8_out, and_9_out,
       and_10_out, and_11_out, and_12_out, and_15_out, and_16_out, and_17_out, and_18_out,
       decodificador_1_add, decodificador_1_lda, decodificador_1_out, decodificador_1_sub,
       sap_1_contador_anel_1_t3, sap_1_contador_anel_1_t4, sap_1_contador_anel_1_t5, sap_1_contador_anel_1_t6;

  decodificador decodificador_1 (
    .Input_0(Input[0]), .Input_1(Input[1]), .Input_2(Input[2]), .Input_3(Input[3]),
    .LDA(decodificador_1_lda), .ADD(decodificador_1_add), .SUB(decodificador_1_sub),
    .OUT(decodificador_1_out), .HLT(HALT));
  sap_1_contador_anel sap_1_contador_anel_1 (
    .Clock(Clock), .Clear(Clear), .T1(EP), .T2(CP), .T3(sap_1_contador_anel_1_t3),
    .T4(sap_1_contador_anel_1_t4), .T5(sap_1_contador_anel_1_t5), .T6(sap_1_contador_anel_1_t6));
  and and_1 (and_1_out, decodificador_1_lda, sap_1_contador_anel_1_t4);
  and and_2 (and_2_out, decodificador_1_add, sap_1_contador_anel_1_t4);
  nor nor_1 (nLM, EP, and_1_out, and_2_out, and_3_out);
  and and_3 (and_3_out, decodificador_1_sub, sap_1_contador_anel_1_t4);
  and and_4 (and_4_out, decodificador_1_lda, sap_1_contador_anel_1_t5);
  and and_5 (and_5_out, decodificador_1_add, sap_1_contador_anel_1_t5);
  nor nor_2 (nCE, sap_1_contador_anel_1_t3, and_4_out, and_5_out, and_6_out);
  and and_6 (and_6_out, decodificador_1_sub, sap_1_contador_anel_1_t5);
  not not_1 (nLi, sap_1_contador_anel_1_t3);
  and and_7 (and_7_out, decodificador_1_lda, sap_1_contador_anel_1_t4);
  and and_8 (and_8_out, decodificador_1_add, sap_1_contador_anel_1_t4);
  nor nor_3 (nEi, and_7_out, and_8_out, and_9_out);
  and and_9 (and_9_out, decodificador_1_sub, sap_1_contador_anel_1_t4);
  and and_10 (and_10_out, decodificador_1_lda, sap_1_contador_anel_1_t5);
  and and_11 (and_11_out, decodificador_1_sub, sap_1_contador_anel_1_t6);
  and and_12 (and_12_out, decodificador_1_add, sap_1_contador_anel_1_t6);
  nor nor_4 (nLA, and_10_out, and_12_out, and_11_out);
  and and_13 (EA, decodificador_1_out, sap_1_contador_anel_1_t4);
  and and_14 (SU, decodificador_1_sub, sap_1_contador_anel_1_t6);
  and and_15 (and_15_out, decodificador_1_add, sap_1_contador_anel_1_t6);
  and and_16 (and_16_out, decodificador_1_sub, sap_1_contador_anel_1_t6);
  or or_1 (EU, and_15_out, and_16_out);
  and and_17 (and_17_out, decodificador_1_add, sap_1_contador_anel_1_t5);
  nor nor_5 (nLB, and_17_out, and_18_out);
  and and_18 (and_18_out, decodificador_1_sub, sap_1_contador_anel_1_t5);
  nand nand_1 (nLo, decodificador_1_out, sap_1_contador_anel_1_t4);
endmodule
